# Fritzing sketch CORE PROJECT SCHEMATIC 1 (saved by Fritzing 0.9.3b)
breadboards: 1

parts:
  LCD1 = LCD screen
  Part3 = Arduino Pro Mini v13
  U29 = L298 [package=multiwatt15]
  M8 = DC Motor
  M9 = DC Motor
  hc-sr1 = hc-sr04  # not connected

nets:
  GND: LCD1.VSS, LCD1.R/W, Part3.GND, U29.GND
  VCC: LCD1.VDD
  N1: LCD1.RS, Part3.A0
  N2: LCD1.E, Part3.A1
  N3: LCD1.DB4, Part3.A2
  N4: LCD1.DB5, Part3.A3
  N5: LCD1.DB6, Part3.A4
  N6: LCD1.DB7, Part3.A5
  5V: Part3.RAW
  N7: Part3.D11_PWM/MOSI, U29.IN4
  N8: Part3.D10_PWM/SS, U29.IN3
  N9: Part3.D9_PWM, U29.IN2
  N10: Part3.D8, U29.IN1
  Echo: Part3.D7
  Trig: Part3.D6_PWM
  N11: U29.OUT1, M9.pin_1
  N12: U29.OUT2, M9.pin_2
  12V: U29.VS
  N13: U29.OUT3, M8.pin_1
  N14: U29.OUT4, M8.pin_2
